// Logisim project 4BitCPU.circ as structural Verilog: 1 circuit, main circuit main
module main (
  input  [19:0] INSTRUCTION,
  input  in_2,
  input  in_3
);

  wire and_1_out, and_2_out, and_3_out, and_4_out, and_5_out, and_6_out, and_7_out, and_8_out, clock_1_out,
       not_1_out, not_2_out, not_3_out, not_4_out;
  wire [3:0] adder_2_out, divider_1_out, multiplexer_1_out, multiplexer_2_out, multiplexer_3_out,
       multiplexer_4_out, multiplier_1_out, progmem_dout, r0_q, r1_q, r2_q, r3_q, subtractor_1_out;
  wire [7:0] adder_1_out, PC_q;
  wire [7:4] progmem_dout_2;
  wire [11:0] progmem_dout_3;

  Clock clock_1 (.out(clock_1_out));
  not not_1 (not_1_out, progmem_dout_3[2]);
  and and_1 (and_1_out, not_1_out, not_2_out);
  not not_2 (not_2_out, progmem_dout_3[3]);
  and and_2 (and_2_out, progmem_dout_3[2], not_3_out);
  not not_3 (not_3_out, progmem_dout_3[3]);
  not not_4 (not_4_out, progmem_dout_3[2]);
  and and_3 (and_3_out, not_4_out, progmem_dout_3[3]);
  and and_4 (and_4_out, progmem_dout_3[2], progmem_dout_3[3]);
  Register #(.width(4)) r0 (.D(multiplexer_4_out), .en(and_5_out), .clk(clock_1_out), .Q(r0_q));  // open: clr
  and and_5 (and_5_out, progmem_dout_3[11], and_1_out);
  Register #(.width(4)) r1 (.D(multiplexer_4_out), .en(and_6_out), .clk(clock_1_out), .Q(r1_q));  // open: clr
  and and_6 (and_6_out, progmem_dout_3[11], and_2_out);
  Register #(.width(4)) r2 (.D(multiplexer_4_out), .en(and_7_out), .clk(clock_1_out), .Q(r2_q));  // open: clr
  and and_7 (and_7_out, progmem_dout_3[11], and_3_out);
  Register #(.width(4)) r3 (.D(multiplexer_4_out), .en(and_8_out), .clk(clock_1_out), .Q(r3_q));  // open: clr
  and and_8 (and_8_out, progmem_dout_3[11], and_4_out);
  Register PC (.D(adder_1_out), .en(clock_1_out), .clk(clock_1_out), .Q(PC_q));  // open: clr
  Adder adder_1 (.a(PC_q), .b(8'h1), .out(adder_1_out));  // open: cin, cout
  Multiplexer #(.select(2), .width(4)) multiplexer_1 (
    .in0(r0_q), .in1(r1_q), .in2(r2_q), .in3(r3_q), .out(multiplexer_1_out), .sel(progmem_dout_3[1:0]));
  Multiplexer #(.select(2), .width(4)) multiplexer_2 (
    .in0(r0_q), .in1(r1_q), .in2(r2_q), .in3(r3_q), .out(multiplexer_2_out), .sel(progmem_dout_3[3:2]));
  Multiplexer #(.width(4)) multiplexer_3 (
    .in0(multiplexer_2_out), .in1(progmem_dout), .out(multiplexer_3_out), .sel(progmem_dout_3[10]));
  Multiplexer #(.select(2), .width(4)) multiplexer_4 (
    .in0(adder_2_out), .in1(subtractor_1_out), .in2(multiplier_1_out), .in3(divider_1_out),
    .out(multiplexer_4_out), .sel(progmem_dout_3[5:4]));
  RAM #(.dataWidth(20)) progmem (
    .addr(PC_q), .we(in_2), .oe(in_3), .clk(clock_1_out), .din(INSTRUCTION),
    .dout({progmem_dout_3, progmem_dout_2, progmem_dout}));
  Adder #(.width(4)) adder_2 (.a(multiplexer_1_out), .b(multiplexer_3_out), .out(adder_2_out));  // open: cin, cout
  Subtractor #(.width(4)) subtractor_1 (
    .a(multiplexer_3_out), .b(multiplexer_1_out), .out(subtractor_1_out));  // open: bin, bout
  Multiplier #(.width(4)) multiplier_1 (
    .a(multiplexer_1_out), .b(multiplexer_3_out), .out(multiplier_1_out));  // open: cin, cout
  Divider #(.width(4)) divider_1 (
    .a(multiplexer_3_out), .b(multiplexer_1_out), .out(divider_1_out));  // open: upper, rem

  // Notes on the sheet:
  //   ALU Output
  //   dest register write selector
  //   register outputs
  //   regsel lines
  //   select immediate
  //   ALU config
  //   Hypothetical Address
endmodule
